// Digital circuit dffOpt.dig as structural Verilog
module dffOpt (
  input  D,
  input  C,
  output Q,
  output Q_2
);

  wire nfet_1_s, nfet_3_s, nfet_7_s, RESET, S_1, S_2, SET;

  NFET nfet_1 (.G(S_2), .D(SET), .S(nfet_1_s));
  NFET nfet_2 (.G(C), .D(nfet_1_s), .S(1'b0));
  PullUp pullup_1 (.out(SET));
  PullUp pullup_2 (.out(S_2));
  NFET nfet_3 (.G(S_1), .D(S_2), .S(nfet_3_s));
  NFET nfet_4 (.G(SET), .D(nfet_3_s), .S(1'b0));
  PullUp pullup_3 (.out(Q));
  NFET nfet_5 (.G(Q_2), .D(Q), .S(nfet_3_s));
  NFET nfet_6 (.G(C), .D(RESET), .S(S_2));
  PullUp pullup_4 (.out(RESET));
  PullUp pullup_5 (.out(S_1));
  NFET nfet_7 (.G(D), .D(S_1), .S(nfet_7_s));
  NFET nfet_8 (.G(RESET), .D(nfet_7_s), .S(1'b0));
  PullUp pullup_6 (.out(Q_2));
  NFET nfet_9 (.G(Q), .D(Q_2), .S(nfet_7_s));

  // Other names for the same wires on the sheet: Q_t = Q_2
endmodule
