// Digital circuit dffRopt.dig as structural Verilog
module dffRopt (
  input  D,
  input  C,
  input  R,
  output Q,
  output Q_2
);

  wire nfet_2_s, nfet_3_s, nfet_5_s, nfet_8_s, R_t, RESET, RESET_t, SET, SET_t;

  NFET nfet_1 (.G(R), .D(R_t), .S(1'b0));
  PullUp pullup_1 (.out(RESET));
  NFET nfet_2 (.G(C), .D(RESET), .S(nfet_2_s));
  NFET nfet_3 (.G(RESET_t), .D(nfet_2_s), .S(nfet_3_s));
  NFET nfet_4 (.G(SET_t), .D(nfet_3_s), .S(1'b0));
  PullUp pullup_2 (.out(RESET_t));
  NFET nfet_5 (.G(D), .D(RESET_t), .S(nfet_5_s));
  NFET nfet_6 (.G(RESET), .D(nfet_5_s), .S(R_t));
  NFET nfet_7 (.G(RESET_t), .D(SET), .S(nfet_3_s));
  PullUp pullup_3 (.out(SET));
  PullUp pullup_4 (.out(SET_t));
  NFET nfet_8 (.G(SET), .D(SET_t), .S(nfet_8_s));
  NFET nfet_9 (.G(C), .D(nfet_8_s), .S(R_t));
  NFET nfet_10 (.G(Q_2), .D(Q), .S(nfet_3_s));
  PullUp pullup_5 (.out(Q));
  PullUp pullup_6 (.out(Q_2));
  NFET nfet_11 (.G(Q), .D(Q_2), .S(nfet_5_s));

  // Other names for the same wires on the sheet: Q_t = Q_2

  // Notes on the sheet:
  //   R: default 1
endmodule
