// Digital circuit dffA.dig as structural Verilog
module dffA (
  input  D,
  input  C,
  input  R,
  input  S,
  output Q,
  output Q_2
);

  wire R_t, S_t, sr2x1_1_out_2;

  sr sr_1 (.S(sr2x1_1_out_2), .R(C), .Out_2(S_t));  // open: Out
  sr2x1 sr2x1_1 (.S__1(S_t), .S__2(C), .R(D), .Out(R_t), .Out_2(sr2x1_1_out_2));
  NFET nfet_1 (.G(S), .D(S_t), .S(1'b0));
  sr sr_2 (.S(S_t), .R(R_t), .Out(Q), .Out_2(Q_2));
  NFET nfet_2 (.G(R), .D(R_t), .S(1'b0));
endmodule
