// Digital circuit tffD.dig as structural Verilog
module tffD (
  input  T,
  input  E,
  input  D,
  output Q,
  output Q_2
);

  wire D_t, nand_1_out, nand_2_out;

  \not  not_1 (.In(D), .Out(D_t));
  tffA tffa_1 (.T(T), .Q(Q), .Q_2(Q_2), .R(nand_1_out), .S(nand_2_out));
  \nand  nand_1 (.In_1(D_t), .In_2(E), .Out(nand_1_out));
  \nand  nand_2 (.In_1(E), .In_2(D), .Out(nand_2_out));
endmodule
