// Digital circuit d.dig as structural Verilog
module d (
  input  D,
  input  E,
  output Q,
  output Q_2
);

  wire D_t;

  \nand  nand_1 (.In_1(E), .In_2(D), .Out(Q_2));
  sr_min sr_min_1 (.S(Q), .R(Q_2), .Q(Q), .Q_2(Q_2));
  \not  not_1 (.In(D), .Out(D_t));
  \nand  nand_2 (.In_1(E), .In_2(D_t), .Out(Q));

  // Other names for the same wires on the sheet: Q_t = Q_2
endmodule
