// Digital circuit counter4.dig as structural Verilog
module counter4 (
  input  C,
  input  R,
  output [3:0] Out,
  output [3:0] Out_2
);

  counter2 counter2_1 (.C(C), .Out(Out[1:0]), .Out_2(Out_2[1:0]), .R(R));
  counter2 counter2_2 (.C(Out_2[1]), .Out(Out[3:2]), .Out_2(Out_2[3:2]), .R(R));

  // Other names for the same wires on the sheet: _0[1:0] = Out[1:0]; _0_t[1:0] = Out_2[1:0]; _1[1:0] = Out[3:2];
  //   _1_t[1:0] = Out_2[3:2]

  // Notes on the sheet:
  //   R: default 1
endmodule
