// Digital circuit binary_clock_hm_sex.dig as structural Verilog
module binary_clock_hm_sex (
  input  clk,
  output [5:0] M,
  output [3:0] H,
  output PM,
  output AM
);

  wire D_PM, H_0_t, H_1_t, H_2_t, H_3_t, H_R, M_0_t, M_1_t, M_2_t, M_3_t, M_4_t, M_5_t, M_R, Set;
  wire [3:0] D_H;
  wire [5:0] D_M;

  DipSwitch dipswitch_1 (.out(D_PM));
  DipSwitch dipswitch_2 (.out(D_H[1]));
  DipSwitch dipswitch_3 (.out(D_H[2]));
  DipSwitch dipswitch_4 (.out(D_H[3]));
  counter6SR counter6sr_1 (
    .C(clk), .D(D_M), .S(Set), .Out(M), .Out_2({M_5_t, M_4_t, M_3_t, M_2_t, M_1_t, M_0_t}), .R(M_R));
  DipSwitch dipswitch_5 (.out(D_M[5]));
  DipSwitch dipswitch_6 (.out(D_H[0]));
  DipSwitch dipswitch_7 (.out(D_M[1]));
  DipSwitch dipswitch_8 (.out(D_M[2]));
  DipSwitch dipswitch_9 (.out(D_M[3]));
  DipSwitch dipswitch_10 (.out(D_M[4]));
  DipSwitch dipswitch_11 (.out(D_M[0]));
  counter4SR counter4sr_1 (.C(M_R), .D(D_H), .S(Set), .Out(H), .Out_2({H_3_t, H_2_t, H_1_t, H_0_t}), .R(H_R));
  nor4 nor4_1 (.In_1(M_2_t), .In_2(M_3_t), .In_3(M_4_t), .In_4(M_5_t), .Out(M_R));
  Button button_1 (.out(Set));
  LED led_1 (.in(PM));
  LED led_2 (.in(AM));
  tffD tffd_1 (.T(H_R), .D(D_PM), .E(Set), .Q(PM), .Q_2(AM));
  \nor  nor_1 (.In_1(H_2_t), .In_2(H_3_t), .Out(H_R));
  LED led_3 (.in(H[3]));
  LED led_4 (.in(H[2]));
  LED led_5 (.in(H[1]));
  LED led_6 (.in(H[0]));
  LED led_7 (.in(M[5]));
  LED led_8 (.in(M[4]));
  LED led_9 (.in(M[3]));
  LED led_10 (.in(M[2]));
  LED led_11 (.in(M[1]));
  LED led_12 (.in(M[0]));

  // Other names for the same wires on the sheet: H_0 = H[0]; H_1 = H[1]; H_2 = H[2]; H_3 = H[3]; M_0 = M[0];
  //   M_1 = M[1]; M_2 = M[2]; M_3 = M[3]; M_4 = M[4]; M_5 = M[5]

  // Notes on the sheet:
  //   PM
  //   AM
  //   Hours
  //   Minutes
  //   Set
  //   32
  //   16
  //   8
  //   4
  //   2
  //   1
endmodule
