// Digital circuit binary_clock_hms_sex.dig as structural Verilog
module binary_clock_hms_sex (
  input  clk,
  output [5:0] S,
  output [5:0] M,
  output [3:0] H,
  output PM,
  output AM
);

  wire and3_1_out, H_0_t, H_1_t, H_2_t, H_3_t, H_R, Inc_H, Inc_M, M_0_t, M_1_t, M_2_t, M_3_t, M_4_t, M_5_t,
       M_R, nand_1_out, nand_2_out, S_0_t, S_1_t, S_2_t, S_3_t, S_4_t, S_5_t, S_R;

  counter6 counter6_1 (.C(clk), .Out(S), .Out_2({S_5_t, S_4_t, S_3_t, S_2_t, S_1_t, S_0_t}), .R(and3_1_out));
  and3 and3_1 (.In_1(S_R), .In_2(Inc_M), .In_3(Inc_H), .Out(and3_1_out));
  \nand  nand_1 (.In_1(Inc_M), .In_2(S_R), .Out(nand_1_out));
  nand4 nand4_1 (.In_1(S[2]), .In_2(S[3]), .In_3(S[4]), .In_4(S[5]), .Out(S_R));
  counter6 counter6_2 (.C(nand_1_out), .Out(M), .Out_2({M_5_t, M_4_t, M_3_t, M_2_t, M_1_t, M_0_t}), .R(M_R));
  \nand  nand_2 (.In_1(Inc_H), .In_2(M_R), .Out(nand_2_out));
  nand4 nand4_2 (.In_1(M[2]), .In_2(M[3]), .In_3(M[4]), .In_4(M[5]), .Out(M_R));
  counter4 counter4_1 (.C(nand_2_out), .Out(H), .Out_2({H_3_t, H_2_t, H_1_t, H_0_t}), .R(H_R));
  Button #(.activeLow("true")) button_1 (.out(Inc_M));
  Button #(.activeLow("true")) button_2 (.out(Inc_H));
  tff tff_1 (.T(H_R), .Q(PM), .Q_2(AM));
  \nand  nand_3 (.In_1(H[2]), .In_2(H[3]), .Out(H_R));
  LED led_1 (.in(PM));
  LED led_2 (.in(AM));
  // RGBLED rgbled_1: pin names not known; wires that end beside it: AM, PM
  // RGBLED rgbled_2: pin names not known; wires that end beside it: AM, PM
  // RGBLED rgbled_3: pin names not known; wires that end beside it: AM, PM
  // RGBLED rgbled_4: pin names not known; wires that end beside it: AM, PM
  // RGBLED rgbled_5: pin names not known; wires that end beside it: AM, PM
  // RGBLED rgbled_6: pin names not known; wires that end beside it: AM, PM
  // RGBLED rgbled_7: pin names not known; wires that end beside it: PM, AM
  // RGBLED rgbled_8: pin names not known; wires that end beside it: PM, AM
  LED led_3 (.in(H[3]));
  LED led_4 (.in(M[5]));
  LED led_5 (.in(M[4]));
  LED led_6 (.in(S[5]));
  LED led_7 (.in(S[4]));
  // RGBLED rgbled_9: pin names not known; wires that end beside it: AM, PM
  // RGBLED rgbled_10: pin names not known; wires that end beside it: AM, PM
  // RGBLED rgbled_11: pin names not known; wires that end beside it: PM, AM
  LED led_8 (.in(H[2]));
  LED led_9 (.in(H[1]));
  LED led_10 (.in(M[3]));
  LED led_11 (.in(M[2]));
  LED led_12 (.in(S[3]));
  LED led_13 (.in(S[2]));
  // RGBLED rgbled_12: pin names not known; wires that end beside it: AM, PM
  // RGBLED rgbled_13: pin names not known; wires that end beside it: PM, AM
  LED led_14 (.in(H[0]));
  LED led_15 (.in(M[1]));
  LED led_16 (.in(M[0]));
  LED led_17 (.in(S[1]));
  LED led_18 (.in(S[0]));
  // RGBLED rgbled_14: pin names not known; wires that end beside it: AM, PM
  // RGBLED rgbled_15: pin names not known; wires that end beside it: PM, AM
  // RGBLED rgbled_16: pin names not known; wires that end beside it: PM, AM
  // RGBLED rgbled_17: pin names not known; wires that end beside it: PM, AM
  // RGBLED rgbled_18: pin names not known; wires that end beside it: PM, AM
  // RGBLED rgbled_19: pin names not known; wires that end beside it: PM, AM
  // RGBLED rgbled_20: pin names not known; wires that end beside it: PM, AM
  // RGBLED rgbled_21: pin names not known; wires that end beside it: PM, AM
  // RGBLED rgbled_22: pin names not known; wires that end beside it: AM, PM

  // Other names for the same wires on the sheet: H_0 = H[0]; H_1 = H[1]; H_2 = H[2]; H_3 = H[3]; M_0 = M[0];
  //   M_1 = M[1]; M_2 = M[2]; M_3 = M[3]; M_4 = M[4]; M_5 = M[5]; S_0 = S[0]; S_1 = S[1]; S_2 = S[2]; S_3 = S[3];
  //   S_4 = S[4]; S_5 = S[5]

  // Notes on the sheet:
  //   Minutes
  //   Hours
  //   PM
  //   AM
  //   8
  //   H
  //   16
  //   32
  //   M
  //   S
  //   2
  //   4
  //   1
endmodule
