// Digital circuit counter_toy.dig as structural Verilog
module counter_toy (
  input  Reset,
  input  In_0,
  input  In_1,
  input  In_2,
  input  In_3,
  input  In_4,
  input  In_5,
  input  In_6,
  input  In_7,
  input  Load_In,
  input  Update,
  output [7:0] D,
  output [7:0] C
);

  wire nm_counter8_resetn_1_ovf, nm_dff_resetn_1_q;

  nm_counter8_resetn nm_counter8_resetn_1 (
    .D({In_7, In_6, In_5, In_4, In_3, In_2, In_1, In_0}), .clk(Update), .set(Load_In), .reset(Reset),
    .Out(C), .ovf(nm_counter8_resetn_1_ovf));
  nm_dff_resetn nm_dff_resetn_1 (
    .D(nm_counter8_resetn_1_ovf), .clk(Update), .r(Reset), .Q(nm_dff_resetn_1_q));  // open: Q_2
  LED Out_0 (.in(C[0]));
  LED Out_1 (.in(C[1]));
  LED Out_2 (.in(C[2]));
  LED Out_3 (.in(C[3]));
  LED Out_4 (.in(C[4]));
  LED Out_5 (.in(C[5]));
  LED Out_6 (.in(C[6]));
  LED Out_7 (.in(C[7]));
  LED Overflow (.in(nm_dff_resetn_1_q));

  assign D = {In_7, In_6, In_5, In_4, In_3, In_2, In_1, In_0};
endmodule
