// Digital circuit counter_toy_simple.dig as structural Verilog
module counter_toy_simple (
  output [3:0] C
);

  wire Count_out, nm_not_1_out, Reset_out;

  Button Count (.out(Count_out));
  Button Reset (.out(Reset_out));
  nm_not nm_not_1 (.In(Reset_out), .Out(nm_not_1_out));
  nm_counter4_resetn nm_counter4_resetn_1 (.clk(Count_out), .Out(C), .r(nm_not_1_out));
  LED Out_0 (.in(C[0]));
  LED Out_1 (.in(C[1]));
  LED Out_2 (.in(C[2]));
  LED Out_3 (.in(C[3]));
endmodule
