// Digital circuit nm_7seg.dig as structural Verilog
module nm_7seg (
  input  [3:0] In,
  output a,
  output b,
  output c,
  output d,
  output e,
  output f,
  output g
);

  wire In_A_t, In_B_t, In_C_t, in_D_t, pullup_1_out, pullup_6_out;

  nc_s2 nc_s2_1 (.In_1(In_B_t), .In_2(in_D_t), .D(pullup_1_out), .S(1'b0));
  nc_s2 nc_s2_2 (.In_1(In_A_t), .In_2(In[1]), .D(pullup_1_out), .S(1'b0));
  nc_s4 nc_s4_1 (.In_1(In_A_t), .In_2(In[2]), .In_3(In_C_t), .In_4(In[0]), .D(b), .S(1'b0));
  nc_s4 nc_s4_2 (.In_1(In_A_t), .In_2(In[2]), .In_3(In_C_t), .In_4(in_D_t), .D(d), .S(1'b0));
  nc_s3 nc_s3_1 (.In_1(In[3]), .In_2(In[2]), .In_3(in_D_t), .D(c), .S(1'b0));
  nc_s3 nc_s3_2 (.In_1(In[3]), .In_2(In_B_t), .In_3(In_C_t), .D(pullup_1_out), .S(1'b0));
  nc_s3 nc_s3_3 (.In_1(In[3]), .In_2(In[2]), .In_3(in_D_t), .D(b), .S(1'b0));
  nc_s4 nc_s4_3 (.In_1(In_A_t), .In_2(In_B_t), .In_3(In_C_t), .In_4(In[0]), .D(d), .S(1'b0));
  PullUp pullup_1 (.out(pullup_1_out));
  nm_not nm_not_1 (.In(pullup_1_out), .Out(a));
  PullUp pullup_2 (.out(b));
  PullUp pullup_3 (.out(c));
  nc_s3 nc_s3_4 (.In_1(In[3]), .In_2(In[2]), .In_3(In[1]), .D(c), .S(1'b0));
  PullUp pullup_4 (.out(d));
  nc_s2 nc_s2_3 (.In_1(In[3]), .In_2(in_D_t), .D(pullup_1_out), .S(1'b0));
  nc_s3 nc_s3_5 (.In_1(In[3]), .In_2(In[1]), .In_3(In[0]), .D(b), .S(1'b0));
  nc_s4 nc_s4_4 (.In_1(In[3]), .In_2(In_B_t), .In_3(In[1]), .In_4(in_D_t), .D(d), .S(1'b0));
  nc_s2 nc_s2_4 (.In_1(In[2]), .In_2(In[1]), .D(pullup_1_out), .S(1'b0));
  nc_s3 nc_s3_6 (.In_1(In[2]), .In_2(In[1]), .In_3(in_D_t), .D(b), .S(1'b0));
  nc_s4 nc_s4_5 (.In_1(In_A_t), .In_2(In_B_t), .In_3(In[1]), .In_4(in_D_t), .D(c), .S(1'b0));
  nc_s3 nc_s3_7 (.In_1(In[2]), .In_2(In[1]), .In_3(In[0]), .D(d), .S(1'b0));
  nc_s2 nc_s2_5 (.In_1(In[3]), .In_2(In_B_t), .D(pullup_6_out), .S(1'b0));
  nc_s3 nc_s3_8 (.In_1(In_A_t), .In_2(In[2]), .In_3(In[0]), .D(pullup_1_out), .S(1'b0));
  nm_not nm_not_2 (.In(In[3]), .Out(In_A_t));
  nc_s2 nc_s2_6 (.In_1(In_A_t), .In_2(In[0]), .D(e), .S(1'b0));
  nc_s3 nc_s3_9 (.In_1(In_A_t), .In_2(In[2]), .In_3(In_C_t), .D(pullup_6_out), .S(1'b0));
  nc_s3 nc_s3_10 (.In_1(In_A_t), .In_2(In_B_t), .In_3(In_C_t), .D(g), .S(1'b0));
  nm_not nm_not_3 (.In(In[2]), .Out(In_B_t));
  nm_not nm_not_4 (.In(In[1]), .Out(In_C_t));
  nm_not nm_not_5 (.In(In[0]), .Out(in_D_t));
  PullUp pullup_5 (.out(e));
  nc_s3 nc_s3_11 (.In_1(In_B_t), .In_2(In_C_t), .In_3(In[0]), .D(e), .S(1'b0));
  PullUp pullup_6 (.out(pullup_6_out));
  nm_not nm_not_6 (.In(pullup_6_out), .Out(f));
  nc_s2 nc_s2_7 (.In_1(In_C_t), .In_2(in_D_t), .D(pullup_6_out), .S(1'b0));
  PullUp pullup_7 (.out(g));
  nc_s4 nc_s4_6 (.In_1(In[3]), .In_2(In[2]), .In_3(In_C_t), .In_4(in_D_t), .D(g), .S(1'b0));
  Seven_Seg seven_seg_1 (.a(a), .b(b), .c(c), .d(d), .e(e), .f(f), .g(g), .dp(1'b0));
  nc_s3 nc_s3_12 (.In_1(In_A_t), .In_2(In[2]), .In_3(In_C_t), .D(e), .S(1'b0));
  nc_s2 nc_s2_8 (.In_1(In[3]), .In_2(In[1]), .D(pullup_6_out), .S(1'b0));
  nc_s4 nc_s4_7 (.In_1(In_A_t), .In_2(In[2]), .In_3(In[1]), .In_4(In[0]), .D(g), .S(1'b0));
  nc_s2 nc_s2_9 (.In_1(In[2]), .In_2(in_D_t), .D(pullup_6_out), .S(1'b0));

  // Other names for the same wires on the sheet: in_D = In[0]; In_C = In[1]; In_B = In[2]; In_A = In[3]

  // Notes on the sheet:
  //   a = B'D' + A'C + AB'C' + AD' + BC + A'BD
  //   b' = A'BC'D + ABD' + ACD + BCD'
  //   c' = ABD' + ABC + A'B'CD'
  //   d' = A'BC'D' + A'B'C'D + AB'CD' + BCD
  //   e' = A'D + B'C'D + A'BC'
  //   f = AB' + A'BC' + C'D' + AC + BD'
  //   g' = A'B'C' + ABC'D' + A'BCD
endmodule
