// Digital circuit nm_ALU_HACK8.dig as structural Verilog
module nm_ALU_HACK8 (
  input  [7:0] X,
  input  [7:0] Y,
  input  zx,
  input  nx,
  input  zy,
  input  ny,
  input  f,
  input  no,
  input  c_in,
  output [7:0] Out,
  output zr,
  output ng,
  output c_out
);

  wire [7:0] nm_and8x_1_out, nm_fulladder8_1_sum, nm_inverter8_1_out, nm_inverter8_2_out, nm_mux8_1_out,
       nm_zero8_1_out, nm_zero8_2_out;

  nm_zero8 nm_zero8_1 (.In(X), .zr(zx), .Out(nm_zero8_1_out));
  nm_Inverter8 nm_inverter8_1 (.In(nm_zero8_1_out), .inv(nx), .Out(nm_inverter8_1_out));
  nm_zero8 nm_zero8_2 (.In(Y), .zr(zy), .Out(nm_zero8_2_out));
  nm_Inverter8 nm_inverter8_2 (.In(nm_zero8_2_out), .inv(ny), .Out(nm_inverter8_2_out));
  nm_And8x nm_and8x_1 (.In_1(nm_inverter8_1_out), .In_2(nm_inverter8_2_out), .Out(nm_and8x_1_out));
  nm_FullAdder8 nm_fulladder8_1 (
    .A(nm_inverter8_1_out), .B(nm_inverter8_2_out), .c_in(c_in), .sum(nm_fulladder8_1_sum), .c_out(c_out));
  nm_mux8 nm_mux8_1 (.A(nm_and8x_1_out), .B(nm_fulladder8_1_sum), .s(f), .Out(nm_mux8_1_out));
  nm_Inverter8 nm_inverter8_3 (.In(nm_mux8_1_out), .inv(no), .Out({ng, Out[6:0]}));
  nm_Nor8 nm_nor8_1 (
    .Out(zr), .In_1(Out[0]), .In_2(Out[1]), .In_3(Out[2]), .In_4(Out[3]), .In_5(Out[4]), .In_6(Out[5]),
    .In_7(Out[6]), .In_8(ng));

  assign Out[7] = ng;
endmodule
