// Digital circuit nm_Or.dig as structural Verilog
module nm_Or (
  input  In_1,
  input  In_2,
  output Out
);

  wire nm_nor_1_out;

  nm_nor nm_nor_1 (.In_1(In_1), .In_2(In_2), .Out(nm_nor_1_out));
  nm_not nm_not_1 (.In(nm_nor_1_out), .Out(Out));
endmodule
