// Digital circuit nm_Xor.dig as structural Verilog
module nm_Xor (
  input  In_1,
  input  In_2,
  output Out
);

  wire nm_nand_1_out, nm_nand_2_out, nm_nand_3_out;

  nm_Nand nm_nand_1 (.In_1(In_1), .In_2(In_2), .Out(nm_nand_1_out));
  nm_Nand nm_nand_2 (.In_1(In_1), .In_2(nm_nand_1_out), .Out(nm_nand_2_out));
  nm_Nand nm_nand_3 (.In_1(nm_nand_1_out), .In_2(In_2), .Out(nm_nand_3_out));
  nm_Nand nm_nand_4 (.In_1(nm_nand_2_out), .In_2(nm_nand_3_out), .Out(Out));
endmodule
