// Digital circuit nm_adder8.dig as structural Verilog
module nm_adder8 (
  input  [7:0] A,
  input  [7:0] B,
  input  c_in,
  output [7:0] sum,
  output c_out,
  output [7:0] \nand 
);

  wire undriven, undriven_2, undriven_3, undriven_4, undriven_5, undriven_6, undriven_7;

  nm_adder nm_adder_1 (.A(A[0]), .B(B[0]), .c_in(c_in));  // open: sum, c_out
  nm_adder nm_adder_2 (.A(A[1]), .B(B[1]), .c_in(undriven));  // open: sum, c_out
  nm_adder nm_adder_3 (.A(A[2]), .B(B[2]), .c_in(undriven_2));  // open: sum, c_out
  nm_adder nm_adder_4 (.A(A[3]), .B(B[3]), .c_in(undriven_3));  // open: sum, c_out
  nm_adder nm_adder_5 (.A(A[4]), .B(B[4]), .c_in(undriven_4));  // open: sum, c_out
  nm_adder nm_adder_6 (.A(A[5]), .B(B[5]), .c_in(undriven_5));  // open: sum, c_out
  nm_adder nm_adder_7 (.A(A[6]), .B(B[6]), .c_in(undriven_6));  // open: sum, c_out
  nm_adder nm_adder_8 (.A(A[7]), .B(B[7]), .c_in(undriven_7));  // open: sum, c_out
endmodule
