// Digital circuit nm_bit.dig as structural Verilog
module nm_bit (
  input  D,
  input  clk,
  input  reset,
  input  en,
  output Out,
  output V
);

  nm_dff nm_dff_1 (.D(D), .clk(clk), .r(reset), .Q(V));  // open: Q_2
  nm_enable nm_enable_1 (.In(V), .en(en), .Out(Out));
endmodule
