// Digital circuit nm_counter4_resetn.dig as structural Verilog
module nm_counter4_resetn (
  input  clk,
  input  r,
  output [3:0] Out,
  output Overflow
);

  wire nm_tff_resetn_1_q_2, nm_tff_resetn_2_q_2, nm_tff_resetn_3_q_2;

  nm_tff_resetn nm_tff_resetn_1 (.T(clk), .Q(Out[0]), .Q_2(nm_tff_resetn_1_q_2), .r(r));
  nm_tff_resetn nm_tff_resetn_2 (.T(nm_tff_resetn_1_q_2), .Q(Out[1]), .Q_2(nm_tff_resetn_2_q_2), .r(r));
  nm_tff_resetn nm_tff_resetn_3 (.T(nm_tff_resetn_2_q_2), .Q(Out[2]), .Q_2(nm_tff_resetn_3_q_2), .r(r));
  nm_tff_resetn nm_tff_resetn_4 (.T(nm_tff_resetn_3_q_2), .Q(Out[3]), .Q_2(Overflow), .r(r));
endmodule
