// Digital circuit nm_counter8_resetn.dig as structural Verilog
module nm_counter8_resetn (
  input  [7:0] D,
  input  clk,
  input  set,
  input  reset,
  output [7:0] Out,
  output ovf
);

  wire notconnected_1_out;
  wire [7:0] nm_adder8_1_sum, nm_mux8_1_out;

  // NotConnected on notconnected_1_out
  nm_adder8 nm_adder8_1 (
    .A(Out), .B(8'h1), .c_in(notconnected_1_out), .sum(nm_adder8_1_sum), .c_out(ovf));  // open: xor, and
  nm_mux8 nm_mux8_1 (.A(nm_adder8_1_sum), .s(set), .B(D), .Out(nm_mux8_1_out));
  nm_byte_resetn nm_byte_resetn_1 (.D(nm_mux8_1_out), .clk(clk), .reset(reset), .Out(Out));  // open: Out_2
endmodule
