// Digital circuit nm_dff.dig as structural Verilog
module nm_dff (
  input  D,
  input  clk,
  input  r,
  output Q,
  output Q_2
);

  wire nm_not_1_out;

  nm_not nm_not_1 (.In(D), .Out(nm_not_1_out));
  nm_jk nm_jk_1 (.J(D), .clk(clk), .K(nm_not_1_out), .r(r), .Q(Q), .Q_2(Q_2));
endmodule
