// Digital circuit nm_dff_asyncn.dig as structural Verilog
module nm_dff_asyncn (
  input  D,
  input  clk,
  input  r,
  input  s,
  output Q,
  output Q_2
);

  wire nm_sr2_2_1_q_2, nm_sr2_2_2_q, nm_sr2_2_2_q_2;

  nm_sr2_2 nm_sr2_2_1 (.s__1(s), .s__2(nm_sr2_2_2_q_2), .r__1(clk), .r__2(r), .Q_2(nm_sr2_2_1_q_2));  // open: Q
  nm_sr2_2 nm_sr2_2_2 (.s__1(nm_sr2_2_1_q_2), .s__2(clk), .r__1(D), .r__2(r), .Q(nm_sr2_2_2_q), .Q_2(nm_sr2_2_2_q_2));
  nm_sr2_2 nm_sr2_2_3 (.s__1(s), .s__2(nm_sr2_2_1_q_2), .r__1(nm_sr2_2_2_q), .r__2(r), .Q(Q), .Q_2(Q_2));
endmodule
