// Digital circuit nm_dff_resetn.dig as structural Verilog
module nm_dff_resetn (
  input  D,
  input  clk,
  input  r,
  output Q,
  output Q_2
);

  wire nm_srn1_2_1_p1, nm_srn1_2_1_p4, nm_srn2_2_1_p5;

  // nm_srn1_2 nm_srn1_2_1: pin names not known; wires that end beside it: nm_srn1_2_1_p1, clk, r, nm_srn1_2_1_p4
  // nm_srn2_2 nm_srn2_2_1: pin names not known; wires that end beside it: nm_srn1_2_1_p4, clk, D, r, nm_srn2_2_1_p5, nm_srn1_2_1_p1
  // nm_srn1_2 nm_srn1_2_2: pin names not known; wires that end beside it: nm_srn1_2_1_p4, nm_srn2_2_1_p5, r, Q, Q_2
endmodule
