// Digital circuit nm_dmux.dig as structural Verilog
module nm_dmux (
  input  In,
  input  sel,
  output Out_1,
  output Out_2
);

  wire nm_not_1_out;

  nm_not nm_not_1 (.In(In), .Out(nm_not_1_out));
  nm_dmuxn nm_dmuxn_1 (.In(nm_not_1_out), .sel(sel), .Out_1(Out_1), .Out_2(Out_2));
endmodule
