// Digital circuit nm_enable.dig as structural Verilog
module nm_enable (
  input  In,
  input  en,
  output Out
);

  wire nfet_1_s, nm_not_1_out, nm_not_2_out, pfet_1_d;

  nm_not nm_not_1 (.In(In), .Out(nm_not_1_out));
  nm_not nm_not_2 (.In(en), .Out(nm_not_2_out));
  PFET pfet_1 (.G(nm_not_1_out), .S(1'b1), .D(pfet_1_d));
  PFET pfet_2 (.G(nm_not_2_out), .S(pfet_1_d), .D(Out));
  NFET nfet_1 (.G(en), .D(Out), .S(nfet_1_s));
  NFET nfet_2 (.G(nm_not_1_out), .D(nfet_1_s), .S(1'b0));
endmodule
