// Digital circuit nm_enableocn8.dig as structural Verilog
module nm_enableocn8 (
  input  [7:0] In,
  input  en,
  output [7:0] Out
);

  nm_enableocn nm_enableocn_1 (.In(In[0]), .en(en), .Out(Out[0]));
  nm_enableocn nm_enableocn_2 (.In(In[1]), .en(en), .Out(Out[1]));
  nm_enableocn nm_enableocn_3 (.In(In[2]), .en(en), .Out(Out[2]));
  nm_enableocn nm_enableocn_4 (.In(In[3]), .en(en), .Out(Out[3]));
  nm_enableocn nm_enableocn_5 (.In(In[4]), .en(en), .Out(Out[4]));
  nm_enableocn nm_enableocn_6 (.In(In[5]), .en(en), .Out(Out[5]));
  nm_enableocn nm_enableocn_7 (.In(In[6]), .en(en), .Out(Out[6]));
  nm_enableocn nm_enableocn_8 (.In(In[7]), .en(en), .Out(Out[7]));
endmodule
