// Digital circuit nm_mux.dig as structural Verilog
module nm_mux (
  input  In_1,
  input  sel,
  input  In_2,
  output Out
);

  wire nm_aoi2x2_1_p5, nm_not_1_out;

  nm_not nm_not_1 (.In(sel), .Out(nm_not_1_out));
  // nm_aoi2x2 nm_aoi2x2_1: pin names not known; wires that end beside it: In_1, nm_not_1_out, In_2, sel, nm_aoi2x2_1_p5
  nm_not nm_not_2 (.In(nm_aoi2x2_1_p5), .Out(Out));
endmodule
