// Digital circuit nm_mux2x4.dig as structural Verilog
module nm_mux2x4 (
  input  A,
  input  [1:0] s,
  input  B,
  input  C,
  input  D,
  output Out
);

  wire nm_aoi2_2_2_2_1_p9, nm_decoder2x4_1_a, nm_decoder2x4_1_b, nm_decoder2x4_1_c, nm_decoder2x4_1_d;

  nm_decoder2x4 nm_decoder2x4_1 (
    .In(s), .A(nm_decoder2x4_1_a), .B(nm_decoder2x4_1_b), .C(nm_decoder2x4_1_c), .D(nm_decoder2x4_1_d));
  // nm_AOI2_2_2_2 nm_aoi2_2_2_2_1: pin names not known; wires that end beside it: A, nm_decoder2x4_1_a, B, nm_decoder2x4_1_b, C, nm_decoder2x4_1_c, D, nm_decoder2x4_1_d, nm_aoi2_2_2_2_1_p9
  nm_Not nm_not_1 (.In(nm_aoi2_2_2_2_1_p9), .Out(Out));
endmodule
