// Digital circuit nm_muxn.dig as structural Verilog
module nm_muxn (
  input  In_1,
  input  sel,
  input  In_2,
  output Out
);

  wire nm_not_1_out;

  nm_not nm_not_1 (.In(sel), .Out(nm_not_1_out));
  // nm_aoi2x2 nm_aoi2x2_1: pin names not known; wires that end beside it: In_1, nm_not_1_out, In_2, sel, Out
endmodule
