// Digital circuit nm_muxn8.dig as structural Verilog
module nm_muxn8 (
  input  [7:0] A,
  input  s,
  input  [7:0] B,
  output [7:0] Out
);

  nm_muxn nm_muxn_1 (.In_1(A[0]), .sel(s), .In_2(B[0]), .Out(Out[0]));
  nm_muxn nm_muxn_2 (.In_1(A[1]), .sel(s), .In_2(B[1]), .Out(Out[1]));
  nm_muxn nm_muxn_3 (.In_1(A[2]), .sel(s), .In_2(B[2]), .Out(Out[2]));
  nm_muxn nm_muxn_4 (.In_1(A[3]), .sel(s), .In_2(B[3]), .Out(Out[3]));
  nm_muxn nm_muxn_5 (.In_1(A[4]), .sel(s), .In_2(B[4]), .Out(Out[4]));
  nm_muxn nm_muxn_6 (.In_1(A[5]), .sel(s), .In_2(B[5]), .Out(Out[5]));
  nm_muxn nm_muxn_7 (.In_1(A[6]), .sel(s), .In_2(B[6]), .Out(Out[6]));
  nm_muxn nm_muxn_8 (.In_1(A[7]), .sel(s), .In_2(B[7]), .Out(Out[7]));
endmodule
