// Digital circuit nm_tff_asyncn.dig as structural Verilog
module nm_tff_asyncn (
  input  T,
  input  r,
  input  s,
  output Q,
  output Q_2
);

  nm_dff_asyncn nm_dff_asyncn_1 (.D(Q_2), .clk(T), .Q(Q), .Q_2(Q_2), .r(r), .s(s));
endmodule
