// Digital circuit nm_xnor.dig as structural Verilog
module nm_xnor (
  input  In_1,
  input  In_2,
  output Out
);

  wire nm_nand_1_out;

  nm_nand nm_nand_1 (.In_1(In_1), .In_2(In_2), .Out(nm_nand_1_out));
  nm_oai2_1 nm_oai2_1_1 (.In_A1(In_2), .In_A2(In_1), .In_B1(nm_nand_1_out), .Out(Out));
endmodule
