// Digital circuit nm_xor.dig as structural Verilog
module nm_xor (
  input  In_1,
  input  In_2,
  output Out
);

  wire nm_nor_1_out;

  nm_nor nm_nor_1 (.In_1(In_1), .In_2(In_2), .Out(nm_nor_1_out));
  nm_aoi2_1 nm_aoi2_1_1 (.In_1(In_2), .In_2(In_1), .In_3(nm_nor_1_out), .Out(Out));
endmodule
